# Fritzing sketch flash_adc-bb (saved by Fritzing 0.9.3b)
breadboards: 1

parts:
  U1 = OP482 - Low Power, High Speed JFET Quad Operational Amplifier [part_number=OP482]
  R1 = Resistor [tolerance=±5% resistance=10k package=THT]
  R2 = Resistor [tolerance=±5% resistance=10k package=THT]
  R3 = Resistor [tolerance=±5% resistance=10k package=THT]
  R4 = Resistor [tolerance=±5% resistance=10k package=THT]
  R5 = Resistor [tolerance=±5% resistance=10k package=THT]

nets:
  N1: U1.-INA, R3.Pin_0, R5.Pin_1
  N2: U1.+INA, U1.+INB, U1.+INC, U1.+IND
  N3: U1.-INB, R3.Pin_1, R4.Pin_0
  N4: U1.-INC, R1.Pin_0, R2.Pin_1
  N5: U1.-IND, R2.Pin_0, R5.Pin_0

notes:
  10kΩ
  W1
  W2
  D3
  D2
  Vp
  Vn
  D1
  D0
  GND
